// Logisim project 16CO235-L2.circ as structural Verilog: 2 circuits, main circuit main
module main (
  input  A3,
  input  A2,
  input  A1,
  input  A0,
  input  B3,
  input  B2,
  input  B1,
  input  B0,
  input  C_in,
  output Carry_Out,
  output S3,
  output S2,
  output S1,
  output S0
);

  wire and_1_out, and_2_out, and_3_out, and_4_out, and_5_out, and_6_out, and_7_out, and_8_out, and_9_out,
       and_10_out, ind_1_generate, ind_1_propogate, ind_2_generate, ind_2_propogate, ind_3_generate,
       ind_3_propogate, ind_4_generate, ind_4_propogate, or_1_out, or_2_out, or_3_out, or_4_out, xor_1_out,
       xor_2_out, xor_3_out, xor_4_out;

  xor xor_1 (xor_1_out, B3, C_in);
  xor xor_2 (xor_2_out, B2, C_in);
  xor xor_3 (xor_3_out, B1, C_in);
  xor xor_4 (xor_4_out, B0, C_in);
  ind ind_1 (.in_1(A3), .in_2(xor_1_out), .Propogate(ind_1_propogate), .Generate(ind_1_generate));
  ind ind_2 (.in_1(A2), .in_2(xor_2_out), .Propogate(ind_2_propogate), .Generate(ind_2_generate));
  ind ind_3 (.in_1(A1), .in_2(xor_3_out), .Propogate(ind_3_propogate), .Generate(ind_3_generate));
  ind ind_4 (.in_1(A0), .in_2(xor_4_out), .Propogate(ind_4_propogate), .Generate(ind_4_generate));
  and and_1 (and_1_out, ind_1_propogate, ind_2_generate);
  and and_2 (and_2_out, ind_1_propogate, ind_2_propogate, ind_3_generate);
  and and_3 (and_3_out, ind_1_propogate, ind_2_propogate, ind_3_propogate, ind_4_generate);
  and and_4 (and_4_out, ind_2_propogate, ind_3_generate);
  and and_5 (and_5_out, ind_2_propogate, ind_4_generate, ind_3_propogate);
  and and_6 (and_6_out, ind_2_propogate, ind_3_propogate, ind_4_propogate, C_in);
  and and_7 (and_7_out, ind_4_generate, ind_3_propogate);
  and and_8 (and_8_out, ind_3_propogate, ind_4_propogate, C_in);
  and and_9 (and_9_out, ind_4_propogate, C_in);
  and and_10 (and_10_out, ind_1_propogate, ind_2_propogate, ind_3_propogate, ind_4_propogate, C_in);
  or or_1 (or_1_out, and_4_out, and_5_out, ind_2_generate, and_6_out);
  or or_2 (or_2_out, and_7_out, ind_3_generate, and_8_out);
  or or_3 (or_3_out, and_9_out, ind_4_generate);
  or or_4 (or_4_out, and_1_out, and_2_out, and_3_out, and_10_out, ind_1_generate);
  xor xor_5 (S3, ind_1_propogate, or_1_out);
  xor xor_6 (S2, ind_2_propogate, or_2_out);
  xor xor_7 (S1, ind_3_propogate, or_3_out);
  xor xor_8 (S0, ind_4_propogate, C_in);
  not not_1 (Carry_Out, or_4_out);

  // Notes on the sheet:
  //   C3
  //   C2
  //   C1
endmodule

module ind (
  input  in_1,
  input  in_2,
  output Propogate,
  output Generate
);

  xor xor_1 (Propogate, in_1, in_2);
  and and_1 (Generate, in_2, in_1);
endmodule
