// Logisim project logisim.circ as structural Verilog: 1 circuit, main circuit main
module main (
  input  Din,
  input  A,
  input  B,
  input  C,
  output Difference,
  output Borrow
);

  wire and_2_out, and_3_out, and_4_out, and_5_out, and_8_out, not_1_out, not_2_out, not_3_out;

  not not_1 (not_1_out, A);
  not not_2 (not_2_out, B);
  not not_3 (not_3_out, C);
  // AND_Gate and_1 has open pins: in0=Din, in1=not_1_out, in2=not_2_out, in3=not_3_out, out=open
  and and_2 (and_2_out, Din, not_1_out, not_2_out, C);
  and and_3 (and_3_out, Din, not_1_out, B, not_3_out);
  and and_4 (and_4_out, Din, not_1_out, B, C);
  and and_5 (and_5_out, Din, A, not_2_out, not_3_out);
  // AND_Gate and_6 has open pins: in0=Din, in1=A, in2=not_2_out, in3=C, out=open
  // AND_Gate and_7 has open pins: in0=Din, in1=A, in2=B, in3=not_3_out, out=open
  and and_8 (and_8_out, Din, A, B, C);
  or or_1 (Difference, and_2_out, and_3_out, and_5_out, and_8_out);
  or or_2 (Borrow, and_2_out, and_3_out, and_4_out, and_8_out);
endmodule
