// Logisim project 16CO235-L4.circ as structural Verilog: 2 circuits, main circuit main
module main (
  input  in_1,
  input  in_2,
  input  in_3,
  input  in_4,
  input  in_5,
  output Y
);

  wire and_1_out, and_2_out, clock_1_out, not_1_out, not_2_out, or_1_out, register_1_q;

  not not_1 (not_1_out, register_1_q);
  or or_1 (or_1_out, register_1_q, Y);
  not not_2 (not_2_out, Y);
  and and_1 (and_1_out, or_1_out, in_1);
  and and_2 (and_2_out, not_2_out, not_1_out, in_1);
  Clock clock_1 (.out(clock_1_out));
  Register register_1 (.D(and_1_out), .Clock_Edge(clock_1_out), .Pre_Set(in_2), .Clear(in_3), .Q(register_1_q));
  Register register_2 (.D(and_2_out), .Clock_Edge(clock_1_out), .Pre_Set(in_4), .Clear(in_5), .Q(Y));

  // Notes on the sheet:
  //   X
  //   Clk
  //   PreSet
  //   Clear
  //   A1
  //   PreSet
  //   Clear
  //   A2
endmodule

// Clear
module Register (
  input  Pre_Set,
  input  D,
  input  Clock_Edge,
  input  Clear,
  output Q
);

  wire nand_1_out, nand_2_out, nand_3_out, nand_4_out, nand_5_out, nand_6_out, nand_8_out, not_1_out,
       not_2_out, not_3_out, not_4_out;

  not not_1 (not_1_out, D);
  nand nand_1 (nand_1_out, nand_8_out, D, Clock_Edge);
  nand nand_2 (nand_2_out, Clock_Edge, not_1_out, Q);
  not not_2 (not_2_out, Clock_Edge);
  not not_3 (not_3_out, Pre_Set);
  not not_4 (not_4_out, Clear);
  nand nand_3 (nand_3_out, nand_1_out, not_3_out, nand_4_out);
  nand nand_4 (nand_4_out, nand_3_out, not_4_out, nand_2_out);
  nand nand_5 (nand_5_out, nand_3_out, not_2_out);
  nand nand_6 (nand_6_out, nand_4_out, not_2_out);
  nand nand_7 (Q, nand_5_out, nand_8_out);
  nand nand_8 (nand_8_out, Q, nand_6_out);

  // Notes on the sheet:
  //   REGISTER
  //   MASTER
  //   SLAVE
endmodule
