// Logisim project Logisim.circ as structural Verilog: 2 circuits, main circuit main
module main (
  input  Input,
  input  Clear,
  input  PreSet,
  output Output
);

  wire clock_1_out, dff_1_q, dff_2_q, dff_3_q;

  Clock clock_1 (.out(clock_1_out));
  DFF dff_1 (.D(Input), .Pre_Set(PreSet), .Clock_Edge(clock_1_out), .Clear(Clear), .Q(dff_1_q));
  DFF dff_2 (.D(dff_1_q), .Pre_Set(PreSet), .Clock_Edge(clock_1_out), .Clear(Clear), .Q(dff_2_q));
  DFF dff_3 (.D(dff_2_q), .Pre_Set(PreSet), .Clock_Edge(clock_1_out), .Clear(Clear), .Q(dff_3_q));
  DFF dff_4 (.D(dff_3_q), .Pre_Set(PreSet), .Clock_Edge(clock_1_out), .Clear(Clear), .Q(Output));

  // Notes on the sheet:
  //   Clk
  //   A1
  //   SHIFT IN SHIFT OUT Register
  //   A2
endmodule

module DFF (
  input  Pre_Set,
  input  D,
  input  Clock_Edge,
  input  Clear,
  output Q
);

  wire nand_1_out, nand_2_out, nand_3_out, nand_4_out, nand_5_out, nand_6_out, nand_8_out, not_1_out,
       not_2_out, not_3_out, not_4_out;

  not not_1 (not_1_out, D);
  not not_2 (not_2_out, Pre_Set);
  nand nand_1 (nand_1_out, nand_8_out, D, Clock_Edge);
  nand nand_2 (nand_2_out, Clock_Edge, not_1_out, Q);
  not not_3 (not_3_out, Clock_Edge);
  not not_4 (not_4_out, Clear);
  nand nand_3 (nand_3_out, nand_1_out, not_2_out, nand_4_out);
  nand nand_4 (nand_4_out, nand_3_out, not_4_out, nand_2_out);
  nand nand_5 (nand_5_out, nand_3_out, not_3_out);
  nand nand_6 (nand_6_out, nand_4_out, not_3_out);
  nand nand_7 (Q, nand_5_out, nand_8_out);
  nand nand_8 (nand_8_out, Q, nand_6_out);

  // Notes on the sheet:
  //   D Flip Flop
  //   MASTER
  //   SLAVE
endmodule
