// Logisim project Logisim.circ as structural Verilog: 1 circuit, main circuit main
module main (
  input  P1,
  input  R1,
  input  P2,
  input  R2,
  input  P3,
  input  R3,
  input  Enable,
  output [2:0] A_B_C,
  output [2:0] A_prime_B_prime_C_prime
);

  wire Clock_out;

  Clock Clock (.out(Clock_out));
  J_K_Flip_Flop j_k_ff_1 (
    .J(A_B_C[1]), .clk(Clock_out), .K(A_B_C[1]), .Q(A_B_C[2]), .Qn(A_prime_B_prime_C_prime[2]), .preset(P1),
    .en(Enable), .reset(R1));
  J_K_Flip_Flop j_k_ff_2 (
    .J(1'b1), .clk(Clock_out), .K(1'b1), .Q(A_B_C[1]), .Qn(A_prime_B_prime_C_prime[1]), .preset(P2),
    .en(Enable), .reset(R2));
  J_K_Flip_Flop j_k_ff_3 (
    .J(1'b1), .clk(Clock_out), .K(A_prime_B_prime_C_prime[2]), .Q(A_B_C[0]), .Qn(A_prime_B_prime_C_prime[0]),
    .preset(P3), .en(Enable), .reset(R3));

  // Notes on the sheet:
  //   Initially Set A,B,C to 001
  //   Some Random Counter
endmodule
